// Logisim project ALU.circ as structural Verilog: 3 circuits, main circuit main
module main (
  input  SUB,
  input  [7:0] in_2,
  input  [7:0] in_3,
  output [7:0] out_4
);

  wire arithmetic_unit_w_flags_1_carry_borrow, arithmetic_unit_w_flags_1_overflow,
       arithmetic_unit_w_flags_1_sign, arithmetic_unit_w_flags_1_zero;

  Arithmetic_Unit_w__Flags arithmetic_unit_w_flags_1 (
    .SUB(SUB), .in_2(in_2), .in_3(in_3), .\Σ (out_4), .ZERO(arithmetic_unit_w_flags_1_zero),
    .Sign(arithmetic_unit_w_flags_1_sign), .Carry_Borrow(arithmetic_unit_w_flags_1_carry_borrow),
    .Overflow(arithmetic_unit_w_flags_1_overflow));
  LED OF (.in(arithmetic_unit_w_flags_1_overflow));
  LED SIGN (.in(arithmetic_unit_w_flags_1_sign));
  LED C_B (.in(arithmetic_unit_w_flags_1_carry_borrow));
  LED ZF (.in(arithmetic_unit_w_flags_1_zero));
endmodule

module Add_Sub_Module (
  input  B0,
  input  B1,
  input  B2,
  input  B3,
  input  SUB,
  input  A0,
  input  A1,
  input  A2,
  input  A3,
  output CO,
  output \Σ0 ,
  output \Σ1 ,
  output \Σ2 ,
  output \Σ3 
);

  wire and_1_out, and_2_out, and_3_out, and_4_out, and_5_out, and_6_out, and_7_out, and_8_out, and_9_out,
       and_10_out, and_11_out, and_12_out, and_13_out, and_14_out, buffer_1_out, buffer_2_out, buffer_3_out,
       buffer_4_out, nand_1_out, nand_2_out, nand_3_out, nand_4_out, nor_1_out, nor_2_out, nor_3_out,
       nor_4_out, nor_5_out, nor_6_out, nor_7_out, not_1_out, not_2_out, not_3_out, not_4_out, not_5_out,
       not_6_out;

  not not_1 (not_1_out, SUB);
  nor nor_1 (nor_1_out, A0, B0);
  not not_2 (not_2_out, nor_1_out);
  not not_3 (not_3_out, not_1_out);
  and and_1 (and_1_out, not_2_out, nand_1_out);
  xor xor_1 (\Σ0 , not_3_out, and_1_out);
  nand nand_1 (nand_1_out, A0, B0);
  and and_2 (and_2_out, not_1_out, nand_1_out);
  buf buffer_1 (buffer_1_out, nor_1_out);
  nor nor_2 (nor_2_out, and_2_out, buffer_1_out);
  xor xor_2 (\Σ1 , nor_2_out, and_3_out);
  nor nor_3 (nor_3_out, A1, B1);
  not not_4 (not_4_out, nor_3_out);
  and and_3 (and_3_out, not_4_out, nand_2_out);
  nand nand_2 (nand_2_out, A1, B1);
  and and_4 (and_4_out, not_1_out, nand_2_out, nand_1_out);
  and and_5 (and_5_out, nand_2_out, nor_1_out);
  nor nor_4 (nor_4_out, and_4_out, and_5_out, buffer_2_out);
  xor xor_3 (\Σ2 , nor_4_out, and_6_out);
  nor nor_5 (nor_5_out, A2, B2);
  not not_5 (not_5_out, nor_5_out);
  buf buffer_2 (buffer_2_out, nor_3_out);
  nand nand_3 (nand_3_out, A2, B2);
  and and_6 (and_6_out, not_5_out, nand_3_out);
  and and_7 (and_7_out, not_1_out, nand_1_out, nand_2_out, nand_3_out);
  nor nor_6 (nor_6_out, A3, B3);
  and and_8 (and_8_out, nand_2_out, nand_3_out, nor_1_out);
  nor nor_7 (nor_7_out, and_7_out, and_8_out, and_9_out, buffer_3_out);
  xor xor_4 (\Σ3 , nor_7_out, and_10_out);
  nand nand_4 (nand_4_out, A3, B3);
  buf buffer_3 (buffer_3_out, nor_5_out);
  and and_9 (and_9_out, nand_3_out, nor_3_out);
  not not_6 (not_6_out, nor_6_out);
  and and_10 (and_10_out, not_6_out, nand_4_out);
  and and_11 (and_11_out, not_1_out, nand_1_out, nand_2_out, nand_3_out, nand_4_out);
  and and_12 (and_12_out, nand_2_out, nand_3_out, nand_4_out, nor_1_out);
  nor nor_8 (CO, and_11_out, and_12_out, and_13_out, and_14_out, buffer_4_out);
  and and_13 (and_13_out, nand_3_out, nor_3_out, nand_4_out);
  and and_14 (and_14_out, nand_4_out, nor_5_out);
  buf buffer_4 (buffer_4_out, nor_6_out);
endmodule

module Arithmetic_Unit_w__Flags (
  input  SUB,
  input  [7:0] in_2,
  input  [7:0] in_3,
  output [7:0] \Σ ,
  output ZERO,
  output Sign,
  output Carry_Borrow,
  output Overflow
);

  wire add_sub_module_1_co, add_sub_module_2_co, and_1_out, and_2_out, and_3_out, and_4_out, and_6_out,
       not_1_out, not_2_out, not_3_out, not_4_out, not_5_out, or_2_out;
  wire [3:0] xor_1_out, xor_5_out;

  LED led_1 (.in(in_2[7]));
  LED led_2 (.in(in_2[6]));
  LED led_3 (.in(in_3[5]));
  LED led_4 (.in(in_3[6]));
  LED led_5 (.in(in_3[7]));
  LED led_6 (.in(in_2[3]));
  LED led_7 (.in(in_2[2]));
  LED led_8 (.in(in_2[4]));
  LED led_9 (.in(in_2[5]));
  LED led_10 (.in(in_3[3]));
  LED led_11 (.in(in_3[4]));
  LED led_12 (.in(in_3[2]));
  LED led_13 (.in(in_3[1]));
  LED led_14 (.in(in_2[1]));
  LED led_15 (.in(in_2[0]));
  LED led_16 (.in(in_3[0]));
  xor xor_1 (xor_1_out[0], in_3[0], SUB);
  xor xor_2 (xor_1_out[1], in_3[1], SUB);
  xor xor_3 (xor_1_out[2], in_3[2], SUB);
  xor xor_4 (xor_1_out[3], in_3[3], SUB);
  xor xor_5 (xor_5_out[0], in_3[4], SUB);
  xor xor_6 (xor_5_out[1], in_3[5], SUB);
  xor xor_7 (xor_5_out[2], in_3[6], SUB);
  xor xor_8 (xor_5_out[3], in_3[7], SUB);
  Add_Sub_Module add_sub_module_1 (
    .A0(in_2[0]), .A1(in_2[1]), .A2(in_2[2]), .A3(in_2[3]), .\Σ0 (\Σ [0]), .\Σ1 (\Σ [1]), .\Σ2 (\Σ [2]),
    .\Σ3 (\Σ [3]), .SUB(SUB), .CO(add_sub_module_1_co), .B0(xor_1_out[0]), .B1(xor_1_out[1]),
    .B2(xor_1_out[2]), .B3(xor_1_out[3]));
  Add_Sub_Module add_sub_module_2 (
    .A0(in_2[4]), .A1(in_2[5]), .A2(in_2[6]), .A3(in_2[7]), .\Σ0 (\Σ [4]), .\Σ1 (\Σ [5]), .\Σ2 (\Σ [6]),
    .\Σ3 (\Σ [7]), .SUB(add_sub_module_1_co), .CO(add_sub_module_2_co), .B0(xor_5_out[0]), .B1(xor_5_out[1]),
    .B2(xor_5_out[2]), .B3(xor_5_out[3]));
  not not_1 (not_1_out, SUB);
  not not_2 (not_2_out, add_sub_module_2_co);
  and and_1 (and_1_out, add_sub_module_2_co, not_1_out);
  and and_2 (and_2_out, not_2_out, SUB);
  or or_1 (Carry_Borrow, and_1_out, and_2_out);
  nor nor_1 (ZERO, \Σ [7], \Σ [6], \Σ [5], \Σ [4], \Σ [3], \Σ [2], \Σ [1], \Σ [0]);
  LED led_17 (.in(\Σ [5]));
  LED led_18 (.in(\Σ [4]));
  LED led_19 (.in(\Σ [7]));
  LED led_20 (.in(\Σ [6]));
  LED led_21 (.in(ZERO));
  LED led_22 (.in(\Σ [3]));
  LED led_23 (.in(\Σ [1]));
  LED led_24 (.in(\Σ [2]));
  LED led_25 (.in(\Σ [0]));
  and and_3 (and_3_out, SUB, \Σ [7]);
  or or_2 (or_2_out, in_3[0], in_3[1], in_3[2], in_3[3], in_3[4], in_3[5], in_3[6], in_3[7]);
  not not_3 (not_3_out, \Σ [7]);
  not not_4 (not_4_out, in_2[7]);
  not not_5 (not_5_out, in_3[7]);
  and and_4 (and_4_out, \Σ [7], not_4_out, not_5_out);
  and and_5 (Sign, and_3_out, or_2_out);
  LED led_26 (.in(Carry_Borrow));
  LED led_27 (.in(Sign));
  and and_6 (and_6_out, not_3_out, in_2[7], in_3[7]);
  LED led_28 (.in(Overflow));
  or or_3 (Overflow, and_6_out, and_4_out);
endmodule
