// Logisim project VGA.circ as structural Verilog: 1 circuit, main circuit main
module main (
  input  MSB,
  input  in_2,
  input  in_3,
  input  in_4,
  input  in_5,
  input  in_6,
  input  in_7,
  input  LSB,
  output HZ_VIS_AREA,
  output HZ_FRONT_PCH
);

  wire and_1_out, and_2_out, and_3_out, and_5_out, and_6_out, and_7_out, and_8_out, not_3_out, not_4_out,
       not_5_out, not_6_out, not_7_out, not_8_out;

  // NOT_Gate not_1 has open pins: in=MSB, out=open
  // NOT_Gate not_2 has open pins: in=in_2, out=open
  not not_3 (not_3_out, in_3);
  not not_4 (not_4_out, in_4);
  not not_5 (not_5_out, in_5);
  not not_6 (not_6_out, in_6);
  not not_7 (not_7_out, in_7);
  not not_8 (not_8_out, LSB);
  and and_1 (and_1_out, MSB, in_2);
  and and_2 (and_2_out, not_3_out, not_4_out);
  and and_3 (and_3_out, in_5, not_6_out);
  // AND_Gate and_4 has open pins: in0=not_5_out, in1=not_6_out, out=open
  and and_5 (and_5_out, not_7_out, not_8_out);
  and and_6 (and_6_out, in_7, not_8_out);
  and and_7 (and_7_out, and_1_out, and_2_out, and_3_out, and_5_out);
  buf and_8 (and_8_out, and_6_out);  // AND_Gate
  // AND_Gate and_9 is placed but not wired
  LED led_1 (.in(and_7_out));
  not not_9 (HZ_VIS_AREA, and_7_out);
  LED led_2 (.in(and_8_out));
  not not_10 (HZ_FRONT_PCH, and_8_out);

  // Notes on the sheet:
  //   11_00_10_00_00
  //   11_01_00_10_00
  //   11_11_00_10_00
  //   1_00_00_10_00_00
  //   11_00_10_00_00
  //   11_01_00_10_00
endmodule
